// Logisim project 02_basicgates.circ as structural Verilog: 1 circuit, main circuit basic gates
module basic_gates (
  input  in_1,
  input  in_2,
  input  in_3,
  input  in_4,
  input  in_5,
  input  in_6,
  input  in_7,
  input  in_8,
  input  in_9,
  input  in_10,
  input  in_11,
  input  in_12,
  input  in_13,
  input  in_14,
  input  in_15,
  input  in_16,
  input  in_17,
  input  in_18,
  input  in_19,
  input  in_20,
  input  in_21,
  input  in_22,
  input  in_23,
  input  in_24
);

  wire and_1_out, and_2_out, and_3_out, and_4_out, or_1_out, or_2_out, or_3_out, or_4_out, xor_1_out,
       xor_2_out, xor_3_out, xor_4_out;

  or or_1 (or_1_out, in_1, in_4);
  LED led_1 (.in(or_1_out));
  or or_2 (or_2_out, in_7, in_10);
  LED led_2 (.in(or_2_out));
  or or_3 (or_3_out, in_13, in_16);
  LED led_3 (.in(or_3_out));
  LED led_4 (.in(or_4_out));
  or or_4 (or_4_out, in_19, in_22);
  LED led_5 (.in(and_1_out));
  and and_1 (and_1_out, in_2, in_5);
  LED led_6 (.in(and_2_out));
  and and_2 (and_2_out, in_8, in_11);
  and and_3 (and_3_out, in_14, in_17);
  LED led_7 (.in(and_3_out));
  and and_4 (and_4_out, in_20, in_23);
  LED led_8 (.in(and_4_out));
  LED led_9 (.in(xor_1_out));
  xor xor_1 (xor_1_out, in_3, in_6);
  xor xor_2 (xor_2_out, in_9, in_12);
  LED led_10 (.in(xor_2_out));
  xor xor_3 (xor_3_out, in_15, in_18);
  LED led_11 (.in(xor_3_out));
  xor xor_4 (xor_4_out, in_21, in_24);
  LED led_12 (.in(xor_4_out));
endmodule
